// Logisim project 20DCE019_DE_Practical_Exam.circ as structural Verilog: 1 circuit, main circuit main
module main (
  input  in_1,
  input  in_2,
  input  in_3,
  input  in_4
);

  wire A_prime_B_prime_out, AB_out, and_1_out, and_2_out, not_1_out, not_2_out, not_3_out, not_4_out,
       or_1_out, or_2_out;

  not not_1 (not_1_out, in_1);
  not not_2 (not_2_out, in_2);
  not not_3 (not_3_out, in_3);
  not not_4 (not_4_out, in_4);
  and and_1 (and_1_out, not_1_out, in_2);
  and and_2 (and_2_out, not_2_out, in_1);
  and AB (AB_out, in_3, in_4);
  and A_prime_B_prime (A_prime_B_prime_out, not_3_out, not_4_out);
  LED led_1 (.in(or_1_out));
  or or_1 (or_1_out, and_1_out, and_2_out);
  or or_2 (or_2_out, AB_out, A_prime_B_prime_out);
  LED led_2 (.in(or_2_out));

  // Notes on the sheet:
  //   XOR
  //   XNOR
  //   A'
  //   B
  //   B'
  //   A
  //   A
  //   B
  //   A'
  //   B'
  //   Y = A'B + AB'
  //   20DCE019
  //   Y = AB+ A'B'
endmodule
