// Logisim project Practical_3.circ as structural Verilog: 1 circuit, main circuit main
module main (
  input  in_1,
  input  in_2,
  input  in_3,
  input  in_4
);

  wire and_1_out, and_2_out, not_1_out, xor_1_out, xor_2_out;

  xor xor_1 (xor_1_out, in_1, in_2);
  and and_1 (and_1_out, in_1, in_2);
  xor xor_2 (xor_2_out, in_3, in_4);
  not not_1 (not_1_out, in_3);
  and and_2 (and_2_out, not_1_out, in_4);
  LED led_1 (.in(xor_1_out));
  LED led_2 (.in(and_1_out));
  LED led_3 (.in(xor_2_out));
  LED led_4 (.in(and_2_out));

  // Notes on the sheet:
  //   A
  //   B
  //   A
  //   B
  //   A
  //   B
  //   A'
  //   B'
  //   sum
  //   carry
  //   difference
  //   Borrow
endmodule
