// Logisim project Practical_5.circ as structural Verilog: 1 circuit, main circuit main
module main (
  input  A,
  input  B,
  input  C
);

  wire and_1_out, and_2_out, and_3_out, or_1_out, xor_1_out;

  ExactlyOne xor_1 (.out(xor_1_out), .in0(A), .in1(B), .in2(C));
  and and_1 (and_1_out, A, B);
  and and_2 (and_2_out, B, C);
  and and_3 (and_3_out, A, C);
  LED led_1 (.in(xor_1_out));
  or or_1 (or_1_out, and_1_out, and_2_out, and_3_out);
  LED led_2 (.in(or_1_out));

  // Notes on the sheet:
  //   ID: 20DCE019
  //   A
  //   B
  //   B
  //   C
  //   A
  //   C
  //   AB
  //   BC
  //   AC
  //   SUM
  //   A xor B xor C
  //   Carry
  //   AB + BC + AC
endmodule
